# Fritzing sketch ckt (saved by Fritzing 1.0.6)

parts:
  U1 = ESP32-38PinWide [part_number=ESP32-38PinWide]
  L298N1 = L298N DC motor driver
  WATER_PUMP1 = water pump/motor
  M1 = DC Motor [voltage_(max)=6V voltage_(min)=3V]
  DS1 = DS18B20 1-Wire Temperature Sensor Probe
  DHT1 = DHT22 Humidity and Temperature Sensor
  Part1 = Arduino Uno (Rev3) - ICSP
  U2 = ESP32-38PinWide [part_number=ESP32-38PinWide]
  HC-SR04_Sensor_1 = HC-SR04 Ultrasonic Distance Sensor
  HC-SR04_Sensor_2 = HC-SR04 Ultrasonic Distance Sensor
  Sensor1 = Gas Sensor Breakout Board
  JACK1 = 2.1mm Barrel Jack with Terminal Block
  YwRobot_Power_Supply1 = YwRobot Breadboard Power Supply [part_number=545043]
  JACK3 = 2.1mm Barrel Jack with Terminal Block
  J1 = female pin header, 2 pins [form="♀ (female)"]
  J2 = Power Jack [package=power_jack_pth_lock]  # not connected

nets:
  N1: U1.GPIO32, L298N1.IN2
  N2: U1.GPIO33, Sensor1.AOUT
  N3: U1.GPIO26, L298N1.IN4
  N4: U1.GPIO27, L298N1.IN1
  N5: U1.GPIO14, L298N1.ENB
  N6: U1.GPIO12, L298N1.IN3
  GND: U1.GND, L298N1.GND, DS1.GND, HC-SR04_Sensor_1.GND, HC-SR04_Sensor_2.GND, Sensor1.GND, JACK1.NEG, YwRobot_Power_Supply1.GND, JACK3.NEG, J1.pin2
  N7: U1.GPIO13, L298N1.ENA
  N8: U1.GPIO15, HC-SR04_Sensor_2.TRIG
  N9: U1.GPIO4, DS1.DQ
  N10: U1.GPIO16, HC-SR04_Sensor_2.ECHO
  N11: U1.GPIO17, HC-SR04_Sensor_1.TRIG
  N12: U1.GPIO18, HC-SR04_Sensor_1.ECHO
  N13: L298N1.OUT1, WATER_PUMP1.pin_1
  N14: L298N1.OUT2, WATER_PUMP1.pin_2
  N15: L298N1.OUT3, M1.pin_2
  N16: L298N1.OUT4, M1.pin_1
  N17: L298N1.12V, JACK1.POS
  VCC: DS1.VDD, HC-SR04_Sensor_2.VCC, YwRobot_Power_Supply1.VCC, J1.pin1
  VDD: DHT1.VDD, Part1.5V
  N18: DHT1.DATA, Part1.D4
  GND_2: DHT1.GND, Part1.GND, U2.GND
  N19: Part1.D0/RX, U2.GPIO17
  N20: Part1.D1/TX, U2.GPIO16
  N21: Sensor1.5V, JACK3.POS

notes:
  12V Supply
  5V Supply
  Water Level indicator
  Hydrometer indicator
  Room Temperature and Humidity
  Cooling Fan
  Water Pump
  Alcohol Detector
  9V Supply
  Liquid Temperature Detector
  Motor Driver

custom parts:
  ESP32-38PinWide: Generic 38-Pin ESP32 with wide format (only access to one side of pins on a breadboard) based on Stephen Lilley's HiLetgo ESP-WROOM-32 ESP32 ESP-32S Development Board.
  L298N DC motor driver: 2x DC motor driver with 78M05 positive voltage regulator (7..35 V) L298N: max 46 V, 2 A Set 5 V Enable jumper to enable 5 V regultor (needed for the L298N) and +5 V output at screw terminal or supply external +5 V at screw terminal Set ENA and/or ENB to +5 V to enable motor permanently or supply ENA and/or ENB with PWM signal IN1 and IN2 set rotation directory for motor A (OUT1/OUT2) IN2 and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
  water pump/motor: WATER PUMP BY ARDUBLOCKTR
  Gas Sensor Breakout Board: Gas sensor breakout board. Input voltage is 5V. Sensor output is available in analog and digital.
  YwRobot Breadboard Power Supply: The YwRobot Breadboard Power Supply (MB-V2) has two power rails; they can be 5V or 3V3. Power to the module can be provided through the female USB socket or through the A10 (female) 2.1mm power jack.
